// Logisim project part2.circ as structural Verilog: 1 circuit, main circuit main
module main (
);

  wire nand_1_out, nand_2_out, nand_3_out, nand_4_out, nand_5_out, nand_6_out, not_1_out, not_2_out,
       not_3_out, not_4_out, not_5_out, not_6_out, undriven, undriven_2, undriven_3, undriven_4;

  not not_1 (not_1_out, undriven_3);
  not not_2 (not_2_out, undriven);
  not not_3 (not_3_out, undriven_4);
  not not_4 (not_4_out, undriven_4);
  not not_5 (not_5_out, undriven_2);
  nand nand_1 (nand_1_out, not_1_out, not_2_out, not_3_out);
  nand nand_2 (nand_2_out, undriven_4, undriven_2);
  nand nand_3 (nand_3_out, undriven, undriven_2);
  nand nand_4 (nand_4_out, undriven_3, not_4_out, not_5_out);
  nand nand_5 (nand_5_out, nand_1_out, nand_2_out, nand_3_out);
  not not_6 (not_6_out, nand_5_out);
  nand nand_6 (nand_6_out, not_6_out, nand_4_out);

  // Notes on the sheet:
  //   a
  //   b
  //   c
  //   d
  //   F(a,b,c,d)
endmodule
