// Logisim project part3.circ as structural Verilog: 1 circuit, main circuit main
module main (
);

  wire undriven_3;
  wire [2:0] undriven_5;
  wire [7:0] multiplexer_1_out, undriven, undriven_2, undriven_4;

  Multiplexer #(.select(3), .width(8)) multiplexer_1 (
    .in0(undriven_2), .in1(undriven), .in2(undriven), .in3(undriven), .in4(undriven_4), .in5(undriven),
    .in6(undriven_2), .in7(undriven_4), .out(multiplexer_1_out), .sel(undriven_5), .en(undriven_3));

  // Notes on the sheet:
  //   d
  //   Logic 1 (5V)
  //   Logic 1 (5V)
  //   Logic 0 (0v)
  //   a
  //   8:1
  //   EN
  //   s
  //   b
  //   F(a,b,c,d
  //   c
endmodule
